# Fritzing sketch eCal connections (saved by Fritzing 0.9.4)

parts:
  M1 = Arduino Nano 33 IOT-tht
  A2 = Waveshare e-Paper HAT [package=THT]

nets:
  N1: M1.pin_1, A2.pin_5
  N2: M1.pin_2, A2.pin_8
  N3: M1.pin_19, A2.pin_7
  N4: M1.pin_22, A2.pin_4
  N5: M1.pin_23, A2.pin_1
  N6: M1.pin_24, A2.pin_2
  N7: M1.pin_25, A2.pin_3
  N8: M1.pin_29, A2.pin_6

custom parts:
  Arduino Nano 33 IOT-tht: The Arduino Nano 33 IoT is the easiest and cheapest point of entry to enhance existing devices (and creating new ones) to be part of the IoT and designing pico-network applications. Whether you are looking at building a sensor network connected to your office or home router, or if you want to create a BLE device sending data to a cellphone, the Nano 33 IoT is your one-stop-solution for many of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
  Waveshare e-Paper HAT: .This is a universal driver board for e-Paper raw panels, can be used to drive various SPI interface e-Paper from Waveshare.
